// Logisim project ALU.circ as structural Verilog: 1 circuit, main circuit main
// ALU
module main (
  input  [15:0] Op1,
  input  [15:0] Op2,
  input  [2:0] SEL,
  output [15:0] ALU_Output,
  output Zero
);

  wire [15:0] adder_1_out, and_1_out, divider_1_out, multiplier_1_out, nand_1_out, or_1_out, subtractor_1_out;

  Adder #(.width(16)) adder_1 (.a(Op1), .b(Op2), .out(adder_1_out));  // open: cin, cout
  Subtractor #(.width(16)) subtractor_1 (.a(Op1), .b(Op2), .out(subtractor_1_out));  // open: bin, bout
  Multiplier #(.width(16)) multiplier_1 (.a(Op1), .b(Op2), .out(multiplier_1_out));  // open: cin, cout
  Divider #(.width(16)) divider_1 (.a(Op1), .b(Op2), .out(divider_1_out));  // open: upper, rem
  assign and_1_out = Op1 & Op2;  // AND_Gate and_1, 16 bits wide
  assign or_1_out = Op1 | Op2;  // OR_Gate or_1, 16 bits wide
  assign nand_1_out = ~(Op1 & Op2);  // NAND_Gate nand_1, 16 bits wide
  and and_2 (Zero, ~ALU_Output[0], ~ALU_Output[1], ~ALU_Output[2], ~ALU_Output[3], ~ALU_Output[4], ~ALU_Output[5], ~ALU_Output[6], ~ALU_Output[7], ~ALU_Output[8], ~ALU_Output[9], ~ALU_Output[10], ~ALU_Output[11], ~ALU_Output[12], ~ALU_Output[13], ~ALU_Output[14], ~ALU_Output[15]);  // AND_Gate
  Multiplexer #(.select(3), .width(16), .enable("false")) multiplexer_1 (
    .in0({16{1'b0}}), .in1(adder_1_out), .in2(subtractor_1_out), .in3(multiplier_1_out), .in4(divider_1_out),
    .in5(and_1_out), .in6(or_1_out), .in7(nand_1_out), .out(ALU_Output), .sel(SEL));

  // Other names for the same wires on the sheet: A[15:0] = ALU_Output
endmodule
