// Logisim project SAMAB.circ as structural Verilog: 1 circuit, main circuit main
module main (
  input  in_1
);

  wire and_1_out, clock_1_out, main_2_alu_src, main_2_branch, main_2_memread, main_2_memtoreg,
       main_2_memwrite, main_2_regdsd, main_2_regwrite, main_4_zero;
  wire [2:0] main_1_opsel, main_2_alu_op;
  wire [3:0] multiplexer_2_out;
  wire [15:0] bit_extender_2_out, main_3_output_1, main_3_output_2, main_4_alu_output, multiplexer_3_out,
       multiplexer_4_out, ram_1_data;
  wire [19:0] adder_1_out, adder_2_out, bit_extender_1_out, multiplexer_1_out, PC_q, rom_1_data;

  Clock clock_1 (.out(clock_1_out));
  assign bit_extender_1_out = {{4{1'b0}}, bit_extender_2_out};  // Bit_Extender bit_extender_1
  Register #(.width(20)) PC (.D(multiplexer_1_out), .Q(PC_q), .clk(clock_1_out), .clr(in_1));  // open: en
  Adder #(.width(20)) adder_1 (.a(20'h1), .b(PC_q), .out(adder_1_out));  // open: cin, cout
  Multiplexer #(.width(20), .enable("false")) multiplexer_1 (
    .in0(adder_1_out), .in1(adder_2_out), .out(multiplexer_1_out), .sel(and_1_out));
  Adder #(.width(20)) adder_2 (.a(bit_extender_1_out), .b(adder_1_out), .out(adder_2_out));  // open: cin, cout
  ROM #(.addrWidth(20), .dataWidth(20)) rom_1 (.addr(PC_q), .data(rom_1_data));  // open: sel
  and and_1 (and_1_out, main_4_zero, main_2_branch);
  Multiplexer #(.width(4), .enable("false")) multiplexer_2 (
    .in0(rom_1_data[11:8]), .in1(rom_1_data[7:4]), .out(multiplexer_2_out), .sel(main_2_regdsd));
  assign bit_extender_2_out = {{8{rom_1_data[7]}}, rom_1_data[7:0]};  // Bit_Extender bit_extender_2
  aluControl_main main_1 (
    .funct(rom_1_data[3:0]),
    .ALUOp_from_control_unit___we_consider_it_3_bits_because_we_have_8to1_mux(main_2_alu_op),
    .opSEL(main_1_opsel));
  controlUnit_main main_2 (
    .ALU_OP_CODE(rom_1_data[19:16]), .branch(main_2_branch), .RegDsd(main_2_regdsd),
    .Alu_src(main_2_alu_src), .RegWrite(main_2_regwrite), .MemRead(main_2_memread),
    .MemToReg(main_2_memtoreg), .MemWrite(main_2_memwrite), .ALU_OP(main_2_alu_op));
  registerFile_main main_3 (
    .Read_Write(main_2_regwrite), .Reg_1(rom_1_data[15:12]), .Reg_2(rom_1_data[11:8]),
    .Destination(multiplexer_2_out), .CLR(in_1), .Input(multiplexer_4_out), .Clock(clock_1_out),
    .Output_1(main_3_output_1), .Output_2(main_3_output_2));
  Multiplexer #(.width(16), .enable("false")) multiplexer_3 (
    .in0(main_3_output_2), .in1(bit_extender_2_out), .out(multiplexer_3_out), .sel(main_2_alu_src));
  ALU_main main_4 (
    .Op1(main_3_output_1), .Op2(multiplexer_3_out), .SEL(main_1_opsel), .ALU_Output(main_4_alu_output),
    .Zero(main_4_zero));
  RAM #(.addrWidth(16), .dataWidth(16), .bus("separate")) ram_1 (
    .addr(main_4_alu_output), .din(main_3_output_2), .data(ram_1_data), .str(main_2_memwrite),
    .clk(clock_1_out), .ld(main_2_memread));  // open: sel, clr
  Multiplexer #(.width(16), .enable("false")) multiplexer_4 (
    .in0(main_4_alu_output), .in1(ram_1_data), .out(multiplexer_4_out), .sel(main_2_memtoreg));

  // Notes on the sheet:
  //   contents of rom_1 (hex, n*v repeats v):
  //   0 10100 10201 1231 3341
endmodule
