// Logisim project aluControl.circ as structural Verilog: 1 circuit, main circuit main
// aluControl
module main (
  input  [3:0] funct,
  input  [2:0] ALUOp_from_control_unit___we_consider_it_3_bits_because_we_have_8to1_mux,
  output [2:0] opSEL
);

  wire [2:0] multiplexer_2_out, multiplexer_3_out, multiplexer_4_out;

  Multiplexer #(.width(3), .enable("false")) multiplexer_1 (
    .in0(multiplexer_4_out), .in1(funct[2:0]), .out(opSEL),
    .sel(ALUOp_from_control_unit___we_consider_it_3_bits_because_we_have_8to1_mux[2]));
  Multiplexer #(.width(3), .enable("false")) multiplexer_2 (
    .in0(3'b000), .in1(3'b010), .out(multiplexer_2_out),
    .sel(ALUOp_from_control_unit___we_consider_it_3_bits_because_we_have_8to1_mux[0]));
  Multiplexer #(.width(3), .enable("false")) multiplexer_3 (
    .in0(3'b000), .in1(3'b001), .out(multiplexer_3_out),
    .sel(ALUOp_from_control_unit___we_consider_it_3_bits_because_we_have_8to1_mux[1]));
  Multiplexer #(.width(3), .enable("false")) multiplexer_4 (
    .in0(multiplexer_2_out), .in1(multiplexer_3_out), .out(multiplexer_4_out),
    .sel(ALUOp_from_control_unit___we_consider_it_3_bits_because_we_have_8to1_mux[1]));
endmodule
