// Logisim project controlUnit.circ as structural Verilog: 1 circuit, main circuit main
// controlUnit
module main (
  input  [3:0] ALU_OP_CODE,
  output branch,
  output RegDsd,
  output Alu_src,
  output RegWrite,
  output MemRead,
  output MemToReg,
  output MemWrite,
  output [2:0] ALU_OP
);

  and R_Type (ALU_OP[2], ~ALU_OP_CODE[3], ~ALU_OP_CODE[2], ~ALU_OP_CODE[1], ~ALU_OP_CODE[0]);  // AND_Gate
  and lw (MemRead, ~ALU_OP_CODE[3], ~ALU_OP_CODE[2], ~ALU_OP_CODE[1], ALU_OP_CODE[0]);  // AND_Gate
  and sw (MemWrite, ALU_OP_CODE[3], ~ALU_OP_CODE[2], ~ALU_OP_CODE[1], ~ALU_OP_CODE[0]);  // AND_Gate
  or or_1 (ALU_OP[1], MemWrite, MemRead);
  and beq (ALU_OP[0], ALU_OP_CODE[3], ~ALU_OP_CODE[2], ~ALU_OP_CODE[1], ALU_OP_CODE[0]);  // AND_Gate
  or or_2 (Alu_src, MemWrite, MemRead);
  or or_3 (RegWrite, MemRead, ALU_OP[2]);

  assign branch = ALU_OP[0];
  assign MemToReg = MemRead;
  assign RegDsd = ALU_OP[2];

  // Other names for the same wires on the sheet: A = ALU_OP[0]
endmodule
