// Logisim project ctrl.circ as structural Verilog: 1 circuit, main circuit main
module main (
  input  [3:0] ALU_OP_CODE,
  input  [2:0] ALU_OP,
  output branch,
  output RegDsd,
  output Alu_src,
  output RegWrite,
  output MemRead,
  output MemToReg,
  output MemWrite
);

  wire ADD_out, AND_out, DIV_out, MUL_out, NAND_out, OR_2_out, SUB_out, XOR_out;

  and ADD (ADD_out, ~ALU_OP_CODE[3], ~ALU_OP_CODE[2], ~ALU_OP_CODE[1], ~ALU_OP_CODE[0]);  // AND_Gate
  and SUB (SUB_out, ~ALU_OP_CODE[3], ~ALU_OP_CODE[2], ~ALU_OP_CODE[1], ALU_OP_CODE[0]);  // AND_Gate
  and MUL (MUL_out, ~ALU_OP_CODE[3], ~ALU_OP_CODE[2], ALU_OP_CODE[1], ~ALU_OP_CODE[0]);  // AND_Gate
  and DIV (DIV_out, ~ALU_OP_CODE[3], ~ALU_OP_CODE[2], ALU_OP_CODE[1], ALU_OP_CODE[0]);  // AND_Gate
  and AND (AND_out, ~ALU_OP_CODE[3], ALU_OP_CODE[2], ~ALU_OP_CODE[1], ~ALU_OP_CODE[0]);  // AND_Gate
  or or_1 (ALU_OP[2], ADD_out, SUB_out, MUL_out, DIV_out, AND_out, OR_2_out, XOR_out, NAND_out);
  and OR_2 (OR_2_out, ~ALU_OP_CODE[3], ALU_OP_CODE[2], ~ALU_OP_CODE[1], ALU_OP_CODE[0]);  // AND_Gate
  and XOR (XOR_out, ~ALU_OP_CODE[3], ALU_OP_CODE[2], ALU_OP_CODE[1], ~ALU_OP_CODE[0]);  // AND_Gate
  and NAND (NAND_out, ~ALU_OP_CODE[3], ALU_OP_CODE[2], ALU_OP_CODE[1], ALU_OP_CODE[0]);  // AND_Gate
  and lw (MemToReg, ALU_OP_CODE[3], ~ALU_OP_CODE[2], ~ALU_OP_CODE[1], ~ALU_OP_CODE[0]);  // AND_Gate
  and sw (MemRead, ALU_OP_CODE[3], ~ALU_OP_CODE[2], ~ALU_OP_CODE[1], ALU_OP_CODE[0]);  // AND_Gate
  or or_3 (ALU_OP[1], MemRead, MemToReg);
  and beq (ALU_OP[0], ALU_OP_CODE[3], ~ALU_OP_CODE[2], ALU_OP_CODE[1], ~ALU_OP_CODE[0]);  // AND_Gate
  or or_4 (Alu_src, MemRead, MemToReg);
  or or_5 (RegWrite, MemToReg, ALU_OP[2]);

  assign branch = ALU_OP[0];
  assign MemWrite = MemRead;
  assign RegDsd = ALU_OP[2];

  // Other names for the same wires on the sheet: A = ALU_OP[0]
endmodule
