// Logisim project registerFile.circ as structural Verilog: 1 circuit, main circuit main
// registerFile
module main (
  input  Read_Write,
  input  [3:0] Reg_1,
  input  [3:0] Reg_2,
  input  [3:0] Destination,
  input  CLR,
  input  [15:0] Input,
  input  Clock,
  output [15:0] Output_1,
  output [15:0] Output_2
);

  wire and_1_out, and_2_out, and_3_out, and_4_out, and_5_out, and_6_out, and_7_out, and_8_out, and_9_out,
       and_10_out, and_11_out, and_12_out, and_13_out, and_14_out, and_15_out, and_16_out,
       demultiplexer_1_out0, demultiplexer_1_out1, demultiplexer_1_out2, demultiplexer_1_out3,
       demultiplexer_1_out4, demultiplexer_1_out5, demultiplexer_1_out6, demultiplexer_1_out7,
       demultiplexer_1_out8, demultiplexer_1_out9, demultiplexer_1_out10, demultiplexer_1_out11,
       demultiplexer_1_out12, demultiplexer_1_out13, demultiplexer_1_out14, demultiplexer_1_out15;
  wire [15:0] register_1_q, register_2_q, register_3_q, register_4_q, register_5_q, register_6_q,
       register_7_q, register_8_q, register_9_q, register_10_q, register_11_q, register_12_q, register_13_q,
       register_14_q, register_15_q, register_16_q, register_17_q;

  Register #(.width(16), .trigger("falling")) register_1 (.D(Input), .Q(register_1_q), .clk(Clock));  // open: en, clr
  Demultiplexer #(.select(4), .enable("false")) demultiplexer_1 (
    .out0(demultiplexer_1_out0), .out1(demultiplexer_1_out1), .out2(demultiplexer_1_out2),
    .out3(demultiplexer_1_out3), .out4(demultiplexer_1_out4), .out5(demultiplexer_1_out5),
    .out6(demultiplexer_1_out6), .out7(demultiplexer_1_out7), .out8(demultiplexer_1_out8),
    .out9(demultiplexer_1_out9), .out10(demultiplexer_1_out10), .out11(demultiplexer_1_out11),
    .out12(demultiplexer_1_out12), .out13(demultiplexer_1_out13), .out14(demultiplexer_1_out14),
    .out15(demultiplexer_1_out15), .in(1'b1), .sel(Destination));
  and and_1 (and_1_out, demultiplexer_1_out0, Read_Write);
  and and_2 (and_2_out, demultiplexer_1_out1, Read_Write);
  and and_3 (and_3_out, demultiplexer_1_out2, Read_Write);
  and and_4 (and_4_out, demultiplexer_1_out3, Read_Write);
  and and_5 (and_5_out, demultiplexer_1_out4, Read_Write);
  and and_6 (and_6_out, demultiplexer_1_out5, Read_Write);
  and and_7 (and_7_out, demultiplexer_1_out6, Read_Write);
  and and_8 (and_8_out, demultiplexer_1_out7, Read_Write);
  and and_9 (and_9_out, demultiplexer_1_out8, Read_Write);
  and and_10 (and_10_out, demultiplexer_1_out9, Read_Write);
  and and_11 (and_11_out, demultiplexer_1_out10, Read_Write);
  and and_12 (and_12_out, demultiplexer_1_out11, Read_Write);
  and and_13 (and_13_out, demultiplexer_1_out12, Read_Write);
  and and_14 (and_14_out, demultiplexer_1_out13, Read_Write);
  and and_15 (and_15_out, demultiplexer_1_out14, Read_Write);
  and and_16 (and_16_out, demultiplexer_1_out15, Read_Write);
  Register #(.width(16), .trigger("high")) register_2 (
    .D(register_1_q), .Q(register_2_q), .clk(and_1_out), .clr(CLR));  // open: en
  Register #(.width(16), .trigger("high")) register_3 (
    .D(register_1_q), .Q(register_3_q), .clk(and_2_out), .clr(CLR));  // open: en
  Register #(.width(16), .trigger("high")) register_4 (
    .D(register_1_q), .Q(register_4_q), .clk(and_3_out), .clr(CLR));  // open: en
  Register #(.width(16), .trigger("high")) register_5 (
    .D(register_1_q), .Q(register_5_q), .clk(and_4_out), .clr(CLR));  // open: en
  Register #(.width(16), .trigger("high")) register_6 (
    .D(register_1_q), .Q(register_6_q), .clk(and_5_out), .clr(CLR));  // open: en
  Register #(.width(16), .trigger("high")) register_7 (
    .D(register_1_q), .Q(register_7_q), .clk(and_6_out), .clr(CLR));  // open: en
  Register #(.width(16), .trigger("high")) register_8 (
    .D(register_1_q), .Q(register_8_q), .clk(and_7_out), .clr(CLR));  // open: en
  Register #(.width(16), .trigger("high")) register_9 (
    .D(register_1_q), .Q(register_9_q), .clk(and_8_out), .clr(CLR));  // open: en
  Register #(.width(16), .trigger("high")) register_10 (
    .D(register_1_q), .Q(register_10_q), .clk(and_9_out), .clr(CLR));  // open: en
  Register #(.width(16), .trigger("high")) register_11 (
    .D(register_1_q), .Q(register_11_q), .clk(and_10_out), .clr(CLR));  // open: en
  Register #(.width(16), .trigger("high")) register_12 (
    .D(register_1_q), .Q(register_12_q), .clk(and_11_out), .clr(CLR));  // open: en
  Register #(.width(16), .trigger("high")) register_13 (
    .D(register_1_q), .Q(register_13_q), .clk(and_12_out), .clr(CLR));  // open: en
  Register #(.width(16), .trigger("high")) register_14 (
    .D(register_1_q), .Q(register_14_q), .clk(and_13_out), .clr(CLR));  // open: en
  Register #(.width(16), .trigger("high")) register_15 (
    .D(register_1_q), .Q(register_15_q), .clk(and_14_out), .clr(CLR));  // open: en
  Register #(.width(16), .trigger("high")) register_16 (
    .D(register_1_q), .Q(register_16_q), .clk(and_15_out), .clr(CLR));  // open: en
  Register #(.width(16), .trigger("high")) register_17 (
    .D(register_1_q), .Q(register_17_q), .clk(and_16_out), .clr(CLR));  // open: en
  Multiplexer #(.select(4), .width(16), .enable("false")) multiplexer_1 (
    .in0(register_2_q), .in1(register_3_q), .in2(register_4_q), .in3(register_5_q), .in4(register_6_q),
    .in5(register_7_q), .in6(register_8_q), .in7(register_9_q), .in8(register_10_q), .in9(register_11_q),
    .in10(register_12_q), .in11(register_13_q), .in12(register_14_q), .in13(register_15_q),
    .in14(register_16_q), .in15(register_17_q), .out(Output_1), .sel(Reg_1));
  Multiplexer #(.select(4), .width(16), .enable("false")) multiplexer_2 (
    .in0(register_2_q), .in1(register_3_q), .in2(register_4_q), .in3(register_5_q), .in4(register_6_q),
    .in5(register_7_q), .in6(register_8_q), .in7(register_9_q), .in8(register_10_q), .in9(register_11_q),
    .in10(register_12_q), .in11(register_13_q), .in12(register_14_q), .in13(register_15_q),
    .in14(register_16_q), .in15(register_17_q), .out(Output_2), .sel(Reg_2));
endmodule
